# Fritzing sketch nfr24l01 con nano (saved by Fritzing 0.9.3b)

parts:
  Transceiver1 = nRF24L01 [package=module]
  Componente1 = Arduino Nano (Rev3.0) (ICSP)
  S1 = Pushbutton [package="[THT]"]
  S2 = Pushbutton [package="[THT]"]
  S3 = Pushbutton [package="[THT]"]
  S4 = Pushbutton [package="[THT]"]
  S5 = Pushbutton [package="[THT]"]
  S6 = Pushbutton [package="[THT]"]
  S7 = Pushbutton [package="[THT]"]
  S8 = Pushbutton [package="[THT]"]
  S9 = Pushbutton [package="[THT]"]
  S10 = Pushbutton [package="[THT]"]
  S11 = Pushbutton [package="[THT]"]
  S12 = Pushbutton [package="[THT]"]
  S13 = Pushbutton [package="[THT]"]
  S14 = Pushbutton [package="[THT]"]

nets:
  GND: Transceiver1.GND, Componente1.GND
  VCC: Transceiver1.VCC, Componente1.3V3
  N1: Transceiver1.CE, Componente1.A2
  N2: Transceiver1.CSN, Componente1.A1
  N3: Transceiver1.SCK, Componente1.D13/SCK
  N4: Transceiver1.MOSI, Componente1.D11/MOSI
  N5: Transceiver1.MISO, Componente1.D12/MISO
  N6: Componente1.D2, S1.Pin_3, S1.Pin_4, S3.Pin_3, S3.Pin_4, S5.Pin_3, S5.Pin_4, S7.Pin_3, S7.Pin_4, S11.Pin_3, S11.Pin_4, S12.Pin_3, S12.Pin_4, S13.Pin_3, S13.Pin_4
  N7: Componente1.D3, S2.Pin_3, S2.Pin_4, S4.Pin_3, S4.Pin_4, S6.Pin_3, S6.Pin_4, S8.Pin_3, S8.Pin_4, S9.Pin_3, S9.Pin_4, S10.Pin_3, S10.Pin_4, S14.Pin_3, S14.Pin_4
  N8: Componente1.D4, S5.Pin_1, S5.Pin_2, S6.Pin_1, S6.Pin_2
  N9: Componente1.D5, S1.Pin_1, S1.Pin_2, S2.Pin_1, S2.Pin_2
  N10: Componente1.D6, S3.Pin_1, S3.Pin_2, S4.Pin_1, S4.Pin_2
  N11: Componente1.D7, S8.Pin_1, S8.Pin_2, S11.Pin_1, S11.Pin_2
  N12: Componente1.D8, S7.Pin_1, S7.Pin_2, S10.Pin_1, S10.Pin_2
  N13: Componente1.D9, S9.Pin_1, S9.Pin_2, S12.Pin_1, S12.Pin_2
  N14: Componente1.D10, S13.Pin_1, S13.Pin_2, S14.Pin_1, S14.Pin_2

custom parts:
  nRF24L01: nRF24L01 module
