# Fritzing sketch nfr24l01 con nano (saved by Fritzing 0.9.3b)

parts:
  Transceiver1 = nRF24L01 [package=module]
  Componente1 = Arduino Nano (Rev3.0) (ICSP)

nets:
  GND: Transceiver1.GND, Componente1.GND
  VCC: Transceiver1.VCC, Componente1.3V3
  N1: Transceiver1.CE, Componente1.A2
  N2: Transceiver1.CSN, Componente1.A1
  N3: Transceiver1.SCK, Componente1.D13/SCK
  N4: Transceiver1.MOSI, Componente1.D11/MOSI
  N5: Transceiver1.MISO, Componente1.D12/MISO

custom parts:
  nRF24L01: nRF24L01 module
